# Fritzing sketch schemaPCB (saved by Fritzing 0.9.3b)
circuit board: 4.33378cm x 3.23915cm
breadboards: 1

parts:
  Componente1 = Arduino Uno (Rev3)
  C1 = Electrolytic Capacitor [capacitance=10µF package="100 mil [THT, electrolytic]"]
  C2 = Electrolytic Capacitor [capacitance=10µF package="100 mil [THT, electrolytic]"]
  Voltage_ref_source = male pin header, 3 pins [form="♂ (male)"]
  IC1 = IC, DIP package, 16 pins [chip_label=IC]
  SW1 = DIP SWITCH [package=dipswitch-02]
  SW2 = DIP SWITCH [package=dipswitch-02]
  R1 = Resistor [tolerance=±5% resistance=220 package=THT]
  R2 = Resistor [tolerance=±5% resistance=220 package=THT]
  R3 = Resistor [tolerance=±5% resistance=220 package=THT]
  J1 = female pin header, 1 pin [form="♀ (female)"]
  Analog_input = female pin header, 4 pins [form="♀ (female)"]
  Voltage_microcontroller_out = female pin header, 2 pins [form="♀ (female)"]
  Voltage_microcontroller_in = female pin header, 2 pins [form="♀ (female)"]
  SDA_SCL = female pin header, 2 pins [form="♀ (female)"]
  J2 = Power Jack [package=power_jack_slot]
  Voltage_ref_out = female pin header, 2 pins [form="♀ (female)"]
  R4 = Resistor [tolerance=±5% resistance=10k package=THT]
  R5 = Resistor [tolerance=±5% resistance=10k package=THT]

nets:
  N1: Componente1.A4/SDA, IC1.pin9, SDA_SCL.pin2, R5.Pin_0
  N2: Componente1.A5/SCL, IC1.pin10, SDA_SCL.pin1, R4.Pin_0
  N3: Componente1.5V, C1.+, Voltage_ref_source.pin1, IC1.pin16, SW1.3, SW1.4, SW2.3, SW2.4, Voltage_microcontroller_out.pin2, Voltage_microcontroller_in.pin2, R4.Pin_1, R5.Pin_1
  GND: Componente1.GND, C1.-, C2.-, IC1.pin8, IC1.pin12, IC1.pin13, R1.Pin_1, R2.Pin_1, R3.Pin_1, Voltage_microcontroller_out.pin1, Voltage_microcontroller_in.pin1, J2.GNDBREAK, J2.GND, Voltage_ref_out.pin1
  N4: C2.+, Voltage_ref_source.pin3, J2.PWR
  N5: Voltage_ref_source.pin2, IC1.pin14, Voltage_ref_out.pin2
  N6: IC1.pin1, Analog_input.pin1
  N7: IC1.pin2, Analog_input.pin2
  N8: IC1.pin3, Analog_input.pin3
  N9: IC1.pin4, Analog_input.pin4
  N10: IC1.pin5, SW2.2, R1.Pin_0
  N11: IC1.pin6, SW1.2, SW2.1, R2.Pin_0
  N12: IC1.pin7, SW1.1, R3.Pin_0
  N13: IC1.pin15, J1.pin1

notes:
  ANA
